// Logisim project ARITMÉTICA 10 BITS TR.circ as structural Verilog: 1 circuit, main circuit main
// ARITMÉTICA TR
module main (
  input  B_9,
  input  A_9,
  input  B_8,
  input  A_8,
  input  B_7,
  input  A_7,
  input  B_6,
  input  A_6,
  input  B_5,
  input  A_5,
  input  B_4,
  input  A_4,
  input  B_3,
  input  A_3,
  input  B_2,
  input  A_2,
  input  B_1,
  input  A_1,
  input  B_0,
  input  A_0,
  input  Cin,
  input  S_0,
  input  S_1,
  output Cout,
  output C_3,
  output Q_9,
  output Q_8,
  output Q_7,
  output Q_6,
  output Q_5,
  output Q_4,
  output Q_3,
  output Q_2,
  output Q_1,
  output Q_0
);

  wire _1_out, main_3_cout, main_4_cout, main_5_cout, main_6_cout, main_7_cout, main_8_cout, main_9_cout,
       main_10_cout, main_11_y;

  SST_TR_main main_1 (.A(A_9), .B(B_9), .S(S_0), .Cin(C_3), .Cout(Cout), .Q(Q_9));
  SST_TR_main main_2 (.A(A_8), .B(B_8), .S(S_0), .Cin(main_3_cout), .Cout(C_3), .Q(Q_8));
  SST_TR_main main_3 (.A(A_7), .B(B_7), .S(S_0), .Cin(main_4_cout), .Cout(main_3_cout), .Q(Q_7));
  SST_TR_main main_4 (.A(A_6), .B(B_6), .S(S_0), .Cin(main_5_cout), .Cout(main_4_cout), .Q(Q_6));
  SST_TR_main main_5 (.A(A_5), .B(B_5), .S(S_0), .Cin(main_6_cout), .Cout(main_5_cout), .Q(Q_5));
  SST_TR_main main_6 (.A(A_4), .B(B_4), .S(S_0), .Cin(main_7_cout), .Cout(main_6_cout), .Q(Q_4));
  SST_TR_main main_7 (.A(A_3), .B(B_3), .S(S_0), .Cin(main_8_cout), .Cout(main_7_cout), .Q(Q_3));
  SST_TR_main main_8 (.A(A_2), .B(B_2), .S(S_0), .Cin(main_9_cout), .Cout(main_8_cout), .Q(Q_2));
  SST_TR_main main_9 (.A(A_1), .B(B_1), .S(S_0), .Cin(main_10_cout), .Cout(main_9_cout), .Q(Q_1));
  SST_TR_main main_10 (.A(A_0), .B(B_0), .S(S_0), .Cin(main_11_y), .Cout(main_10_cout), .Q(Q_0));
  not _1 (_1_out, Cin);
  MUX_3_X_1_TR_main main_11 (.E_2(S_0), .E_3(Cin), .E_4(_1_out), .S_O(S_0), .S_1(S_1), .Y(main_11_y));
endmodule
