// Logisim project BIT A BIT 10 BITS TR.circ as structural Verilog: 1 circuit, main circuit main
// BIT A BIT TR
module main (
  input  B_9,
  input  A_9,
  input  B_8,
  input  A_8,
  input  B_7,
  input  A_7,
  input  B_6,
  input  A_6,
  input  B_5,
  input  A_5,
  input  B_4,
  input  A_4,
  input  B_3,
  input  A_3,
  input  B_2,
  input  A_2,
  input  B_1,
  input  A_1,
  input  B_0,
  input  A_0,
  output XOR_9,
  output XOR_8,
  output XOR_7,
  output NOR_9,
  output XOR_6,
  output XOR_5,
  output NOR_8,
  output NAND_9,
  output XOR_4,
  output NOR_7,
  output NAND_8,
  output XOR_3,
  output NOR_6,
  output NAND_7,
  output XOR_2,
  output NOR_5,
  output NAND_6,
  output XOR_1,
  output NOR_4,
  output NAND_5,
  output XOR_0,
  output NOR_3,
  output NAND_4,
  output NOR_2,
  output NAND_3,
  output NAND_2,
  output NOR_1,
  output NAND_1,
  output NOR_0,
  output NAND_0
);

  BIT_BIT_TR_main main_1 (.A(A_9), .B(B_9), .NAND(NAND_9), .NOR(NOR_9), .XOR(XOR_9));
  BIT_BIT_TR_main main_2 (.A(A_8), .B(B_8), .NAND(NAND_8), .NOR(NOR_8), .XOR(XOR_8));
  BIT_BIT_TR_main main_3 (.A(A_7), .B(B_7), .NAND(NAND_7), .NOR(NOR_7), .XOR(XOR_7));
  BIT_BIT_TR_main main_4 (.A(A_6), .B(B_6), .NAND(NAND_6), .NOR(NOR_6), .XOR(XOR_6));
  BIT_BIT_TR_main main_5 (.A(A_5), .B(B_5), .NAND(NAND_5), .NOR(NOR_5), .XOR(XOR_5));
  BIT_BIT_TR_main main_6 (.A(A_4), .B(B_4), .NAND(NAND_4), .NOR(NOR_4), .XOR(XOR_4));
  BIT_BIT_TR_main main_7 (.A(A_3), .B(B_3), .NAND(NAND_3), .NOR(NOR_3), .XOR(XOR_3));
  BIT_BIT_TR_main main_8 (.A(A_2), .B(B_2), .NAND(NAND_2), .NOR(NOR_2), .XOR(XOR_2));
  BIT_BIT_TR_main main_9 (.A(A_1), .B(B_1), .NAND(NAND_1), .NOR(NOR_1), .XOR(XOR_1));
  BIT_BIT_TR_main main_10 (.A(A_0), .B(B_0), .NAND(NAND_0), .NOR(NOR_0), .XOR(XOR_0));
endmodule
