// Logisim project BIT BIT TR.circ as structural Verilog: 1 circuit, main circuit main
// BIT
module main (
  input  A,
  input  B,
  output NAND,
  output NOR,
  output XOR
);

  wire transistor_4_out, transistor_6_out, transistor_12_out;

  Transistor transistor_1 (.in(1'b1), .out(NAND), .gate(B));
  Transistor transistor_2 (.in(1'b1), .out(NAND), .gate(A));
  Transistor #(.\type ("n")) transistor_3 (.in(transistor_4_out), .out(NAND), .gate(A));
  Transistor #(.\type ("n")) transistor_4 (.in(1'b0), .out(transistor_4_out), .gate(B));
  Transistor #(.\type ("n")) transistor_5 (.in(1'b0), .out(NOR), .gate(A));
  Transistor transistor_6 (.in(1'b1), .out(transistor_6_out), .gate(A));
  Transistor transistor_7 (.in(transistor_6_out), .out(NOR), .gate(B));
  Transistor #(.\type ("n")) transistor_8 (.in(1'b0), .out(NOR), .gate(B));
  Transistor #(.gate("br")) transistor_9 (.in(A), .out(XOR), .gate(B));
  Transistor transistor_10 (.in(B), .out(XOR), .gate(A));
  Transistor #(.\type ("n")) transistor_11 (.in(transistor_12_out), .out(XOR), .gate(A));
  Transistor #(.\type ("n")) transistor_12 (.in(1'b0), .out(transistor_12_out), .gate(B));
endmodule
