// Logisim project COMPARADOR 10 BITS.circ as structural Verilog: 1 circuit, main circuit main
// COMPARADOR TR
module main (
  input  B9,
  input  B8,
  input  B7,
  input  B6,
  input  B5,
  input  B4,
  input  B3,
  input  B2,
  input  B1,
  input  B0,
  input  A9,
  input  A8,
  input  A7,
  input  A6,
  input  A5,
  input  A4,
  input  A3,
  input  A2,
  input  A1,
  input  A0,
  input  Q9,
  input  Q8,
  input  Q7,
  input  Q6,
  input  Q5,
  input  Q4,
  input  Q3,
  input  Q2,
  input  Q1,
  input  Q0,
  input  C_8,
  input  Cout,
  output OVER_FLOW,
  output B___0,
  output A___0,
  output A___B,
  output A___B_2,
  output A___B_3
);

  wire transistor_5_out, transistor_9_out, transistor_12_out, transistor_13_out, transistor_14_out,
       transistor_15_out, transistor_16_out, transistor_17_out, transistor_20_out, transistor_21_out,
       transistor_26_out, transistor_27_out, transistor_28_out, transistor_29_out, transistor_30_out,
       transistor_37_out, transistor_38_out, transistor_40_out, transistor_41_out, transistor_46_out,
       transistor_47_out, transistor_48_out, transistor_49_out, transistor_50_out, transistor_54_out,
       transistor_56_out, transistor_57_out, transistor_63_out, transistor_64_out, transistor_68_out,
       transistor_69_out, transistor_70_out, transistor_71_out, transistor_77_out, transistor_78_out,
       transistor_84_out, transistor_87_out, transistor_88_out, transistor_89_out, transistor_90_out,
       transistor_91_out, transistor_96_out, transistor_97_out, transistor_98_out, transistor_99_out;

  Transistor #(.\type ("n")) transistor_1 (.in(1'b0), .out(B___0), .gate(B8));
  Transistor #(.gate("br")) transistor_2 (.in(C_8), .out(OVER_FLOW), .gate(Cout));
  Transistor transistor_3 (.in(Cout), .out(OVER_FLOW), .gate(C_8));
  Transistor #(.\type ("n")) transistor_4 (.in(transistor_5_out), .out(OVER_FLOW), .gate(Cout));
  Transistor #(.\type ("n")) transistor_5 (.in(1'b0), .out(transistor_5_out), .gate(C_8));
  Transistor #(.\type ("n")) transistor_6 (.in(1'b0), .out(B___0), .gate(B6));
  Transistor #(.\type ("n")) transistor_7 (.in(1'b0), .out(B___0), .gate(B2));
  Transistor #(.\type ("n")) transistor_8 (.in(1'b0), .out(B___0), .gate(B4));
  Transistor #(.gate("br")) transistor_9 (.in(A9), .out(transistor_9_out), .gate(B9));
  Transistor transistor_10 (.in(B9), .out(transistor_9_out), .gate(A9));
  Transistor #(.\type ("n")) transistor_11 (.in(transistor_12_out), .out(transistor_9_out), .gate(B9));
  Transistor #(.\type ("n")) transistor_12 (.in(1'b0), .out(transistor_12_out), .gate(A9));
  Transistor transistor_13 (.in(1'b1), .out(transistor_13_out), .gate(B0));
  Transistor transistor_14 (.in(transistor_13_out), .out(transistor_14_out), .gate(B2));
  Transistor transistor_15 (.in(transistor_14_out), .out(transistor_15_out), .gate(B4));
  Transistor transistor_16 (.in(transistor_15_out), .out(transistor_16_out), .gate(B6));
  Transistor transistor_17 (.in(transistor_16_out), .out(transistor_17_out), .gate(B8));
  Transistor #(.\type ("n")) transistor_18 (.in(1'b0), .out(B___0), .gate(B9));
  Transistor #(.\type ("n")) transistor_19 (.in(1'b0), .out(B___0), .gate(B0));
  Transistor transistor_20 (.in(1'b1), .out(transistor_20_out), .gate(transistor_9_out));
  Transistor transistor_21 (.in(1'b1), .out(transistor_21_out), .gate(A___B));
  Transistor #(.\type ("n")) transistor_22 (.in(1'b0), .out(transistor_20_out), .gate(transistor_9_out));
  Transistor #(.\type ("n")) transistor_23 (.in(1'b0), .out(transistor_21_out), .gate(A___B));
  Transistor #(.\type ("n")) transistor_24 (.in(1'b0), .out(B___0), .gate(B7));
  Transistor #(.\type ("n")) transistor_25 (.in(1'b0), .out(B___0), .gate(B5));
  Transistor transistor_26 (.in(1'b1), .out(transistor_26_out), .gate(transistor_21_out));
  Transistor transistor_27 (.in(transistor_17_out), .out(transistor_27_out), .gate(B1));
  Transistor transistor_28 (.in(transistor_27_out), .out(transistor_28_out), .gate(B3));
  Transistor transistor_29 (.in(transistor_28_out), .out(transistor_29_out), .gate(B5));
  Transistor transistor_30 (.in(transistor_29_out), .out(transistor_30_out), .gate(B7));
  Transistor transistor_31 (.in(transistor_30_out), .out(B___0), .gate(B9));
  Transistor #(.\type ("n")) transistor_32 (.in(1'b0), .out(B___0), .gate(B1));
  Transistor #(.\type ("n")) transistor_33 (.in(1'b0), .out(B___0), .gate(B3));
  Transistor transistor_34 (.in(1'b1), .out(transistor_26_out), .gate(transistor_20_out));
  Transistor transistor_35 (.in(1'b1), .out(transistor_26_out), .gate(Cout));
  Transistor #(.\type ("n")) transistor_36 (.in(transistor_37_out), .out(transistor_26_out), .gate(transistor_21_out));
  Transistor #(.\type ("n")) transistor_37 (.in(transistor_38_out), .out(transistor_37_out), .gate(transistor_20_out));
  Transistor #(.\type ("n")) transistor_38 (.in(1'b0), .out(transistor_38_out), .gate(Cout));
  Transistor #(.\type ("n")) transistor_39 (.in(1'b0), .out(A___0), .gate(A8));
  Transistor transistor_40 (.in(1'b1), .out(transistor_40_out), .gate(transistor_41_out));
  Transistor transistor_41 (.in(1'b1), .out(transistor_41_out), .gate(A9));
  Transistor #(.\type ("n")) transistor_42 (.in(1'b0), .out(transistor_41_out), .gate(A9));
  Transistor #(.\type ("n")) transistor_43 (.in(1'b0), .out(A___0), .gate(A4));
  Transistor #(.\type ("n")) transistor_44 (.in(1'b0), .out(A___0), .gate(A6));
  Transistor transistor_45 (.in(1'b1), .out(transistor_40_out), .gate(B9));
  Transistor transistor_46 (.in(1'b1), .out(transistor_46_out), .gate(A0));
  Transistor transistor_47 (.in(transistor_46_out), .out(transistor_47_out), .gate(A2));
  Transistor transistor_48 (.in(transistor_47_out), .out(transistor_48_out), .gate(A4));
  Transistor transistor_49 (.in(transistor_48_out), .out(transistor_49_out), .gate(A6));
  Transistor transistor_50 (.in(transistor_49_out), .out(transistor_50_out), .gate(A8));
  Transistor #(.\type ("n")) transistor_51 (.in(1'b0), .out(A___0), .gate(A2));
  Transistor #(.\type ("n")) transistor_52 (.in(1'b0), .out(A___0), .gate(A0));
  Transistor transistor_53 (.in(1'b1), .out(transistor_40_out), .gate(transistor_21_out));
  Transistor transistor_54 (.in(1'b1), .out(transistor_54_out), .gate(B9));
  Transistor #(.\type ("n")) transistor_55 (.in(transistor_56_out), .out(transistor_40_out), .gate(transistor_41_out));
  Transistor #(.\type ("n")) transistor_56 (.in(transistor_57_out), .out(transistor_56_out), .gate(B9));
  Transistor #(.\type ("n")) transistor_57 (.in(1'b0), .out(transistor_57_out), .gate(transistor_21_out));
  Transistor #(.\type ("n")) transistor_58 (.in(1'b0), .out(A___0), .gate(A7));
  Transistor #(.\type ("n")) transistor_59 (.in(1'b0), .out(A___0), .gate(A9));
  Transistor transistor_60 (.in(1'b1), .out(transistor_54_out), .gate(transistor_21_out));
  Transistor transistor_61 (.in(1'b1), .out(transistor_54_out), .gate(transistor_41_out));
  Transistor #(.\type ("n")) transistor_62 (.in(transistor_63_out), .out(transistor_54_out), .gate(B9));
  Transistor #(.\type ("n")) transistor_63 (.in(transistor_64_out), .out(transistor_63_out), .gate(transistor_41_out));
  Transistor #(.\type ("n")) transistor_64 (.in(1'b0), .out(transistor_64_out), .gate(transistor_21_out));
  Transistor #(.\type ("n")) transistor_65 (.in(1'b0), .out(A___0), .gate(A5));
  Transistor #(.\type ("n")) transistor_66 (.in(1'b0), .out(A___0), .gate(A3));
  Transistor transistor_67 (.in(1'b1), .out(A___B_2), .gate(transistor_40_out));
  Transistor transistor_68 (.in(transistor_50_out), .out(transistor_68_out), .gate(A1));
  Transistor transistor_69 (.in(transistor_68_out), .out(transistor_69_out), .gate(A3));
  Transistor transistor_70 (.in(transistor_69_out), .out(transistor_70_out), .gate(A5));
  Transistor transistor_71 (.in(transistor_70_out), .out(transistor_71_out), .gate(A7));
  Transistor transistor_72 (.in(transistor_71_out), .out(A___0), .gate(A9));
  Transistor #(.\type ("n")) transistor_73 (.in(1'b0), .out(A___0), .gate(A1));
  Transistor transistor_74 (.in(1'b1), .out(A___B_2), .gate(transistor_54_out));
  Transistor transistor_75 (.in(1'b1), .out(A___B_2), .gate(transistor_26_out));
  Transistor #(.\type ("n")) transistor_76 (.in(transistor_77_out), .out(A___B_2), .gate(transistor_26_out));
  Transistor #(.\type ("n")) transistor_77 (.in(transistor_78_out), .out(transistor_77_out), .gate(transistor_54_out));
  Transistor #(.\type ("n")) transistor_78 (.in(1'b0), .out(transistor_78_out), .gate(transistor_40_out));
  Transistor #(.\type ("n")) transistor_79 (.in(1'b0), .out(A___B), .gate(Q6));
  Transistor #(.\type ("n")) transistor_80 (.in(1'b0), .out(A___B), .gate(Q8));
  Transistor transistor_81 (.in(1'b1), .out(A___B_3), .gate(A___B));
  Transistor transistor_82 (.in(1'b1), .out(A___B_3), .gate(A___B_2));
  Transistor #(.\type ("n")) transistor_83 (.in(transistor_84_out), .out(A___B_3), .gate(A___B_2));
  Transistor #(.\type ("n")) transistor_84 (.in(1'b0), .out(transistor_84_out), .gate(A___B));
  Transistor #(.\type ("n")) transistor_85 (.in(1'b0), .out(A___B), .gate(Q4));
  Transistor #(.\type ("n")) transistor_86 (.in(1'b0), .out(A___B), .gate(Q2));
  Transistor transistor_87 (.in(1'b1), .out(transistor_87_out), .gate(Q0));
  Transistor transistor_88 (.in(transistor_87_out), .out(transistor_88_out), .gate(Q2));
  Transistor transistor_89 (.in(transistor_88_out), .out(transistor_89_out), .gate(Q4));
  Transistor transistor_90 (.in(transistor_89_out), .out(transistor_90_out), .gate(Q6));
  Transistor transistor_91 (.in(transistor_90_out), .out(transistor_91_out), .gate(Q8));
  Transistor #(.\type ("n")) transistor_92 (.in(1'b0), .out(A___B), .gate(Q0));
  Transistor #(.\type ("n")) transistor_93 (.in(1'b0), .out(A___B), .gate(Q9));
  Transistor #(.\type ("n")) transistor_94 (.in(1'b0), .out(A___B), .gate(Q7));
  Transistor #(.\type ("n")) transistor_95 (.in(1'b0), .out(A___B), .gate(Q5));
  Transistor transistor_96 (.in(transistor_91_out), .out(transistor_96_out), .gate(Q1));
  Transistor transistor_97 (.in(transistor_96_out), .out(transistor_97_out), .gate(Q3));
  Transistor transistor_98 (.in(transistor_97_out), .out(transistor_98_out), .gate(Q5));
  Transistor transistor_99 (.in(transistor_98_out), .out(transistor_99_out), .gate(Q7));
  Transistor transistor_100 (.in(transistor_99_out), .out(A___B), .gate(Q9));
  Transistor #(.\type ("n")) transistor_101 (.in(1'b0), .out(A___B), .gate(Q3));
  Transistor #(.\type ("n")) transistor_102 (.in(1'b0), .out(A___B), .gate(Q1));

  // Notes on the sheet:
  //   9
  //   10
  //   4
  //   11
  //   5
  //   6
  //   8
  //   7
endmodule
