// Logisim project FIM TR.circ as structural Verilog: 1 circuit, main circuit main
// FIM
module main (
  input  D_9,
  input  S_0,
  input  S_1,
  input  DY_ANTERIOR,
  output S1,
  output NOT_S1,
  output YD_ANTERIOR,
  output Y
);

  wire transistor_2_out, transistor_5_out, transistor_7_out, transistor_8_out, transistor_12_out;

  Transistor #(.\type ("n")) transistor_1 (.in(1'b0), .out(YD_ANTERIOR), .gate(NOT_S1));
  Transistor transistor_2 (.in(1'b1), .out(transistor_2_out), .gate(NOT_S1));
  Transistor transistor_3 (.in(transistor_2_out), .out(YD_ANTERIOR), .gate(D_9));
  Transistor #(.\type ("n")) transistor_4 (.in(1'b0), .out(YD_ANTERIOR), .gate(D_9));
  Transistor #(.\type ("n")) transistor_5 (.in(1'b0), .out(transistor_5_out), .gate(D_9));
  Transistor #(.\type ("n")) transistor_6 (.in(1'b0), .out(transistor_5_out), .gate(S_0));
  Transistor transistor_7 (.in(1'b1), .out(transistor_7_out), .gate(D_9));
  Transistor transistor_8 (.in(transistor_7_out), .out(transistor_8_out), .gate(S_0));
  Transistor transistor_9 (.in(transistor_8_out), .out(transistor_5_out), .gate(NOT_S1));
  Transistor #(.\type ("n")) transistor_10 (.in(1'b0), .out(transistor_5_out), .gate(NOT_S1));
  Transistor #(.\type ("n")) transistor_11 (.in(1'b0), .out(Y), .gate(transistor_5_out));
  Transistor transistor_12 (.in(1'b1), .out(transistor_12_out), .gate(transistor_5_out));
  Transistor transistor_13 (.in(transistor_12_out), .out(Y), .gate(DY_ANTERIOR));
  Transistor #(.\type ("n")) transistor_14 (.in(1'b0), .out(Y), .gate(DY_ANTERIOR));
  Transistor transistor_15 (.in(1'b1), .out(NOT_S1), .gate(S_1));
  Transistor #(.\type ("n")) transistor_16 (.in(1'b0), .out(NOT_S1), .gate(S_1));

  assign S1 = S_1;
endmodule
