// Logisim project INÍCIO TR.circ as structural Verilog: 1 circuit, main circuit main
// INÍCIO
module main (
  input  D_0,
  input  S_1,
  input  NOT_S_1,
  input  \YD_PRÓXIMO ,
  output \DY_PRÓXIMO ,
  output Y_0
);

  wire transistor_2_out, transistor_6_out;

  Transistor #(.\type ("n")) transistor_1 (.in(1'b0), .out(\DY_PRÓXIMO ), .gate(S_1));
  Transistor transistor_2 (.in(1'b1), .out(transistor_2_out), .gate(S_1));
  Transistor transistor_3 (.in(transistor_2_out), .out(\DY_PRÓXIMO ), .gate(D_0));
  Transistor #(.\type ("n")) transistor_4 (.in(1'b0), .out(Y_0), .gate(NOT_S_1));
  Transistor #(.\type ("n")) transistor_5 (.in(1'b0), .out(\DY_PRÓXIMO ), .gate(D_0));
  Transistor transistor_6 (.in(1'b1), .out(transistor_6_out), .gate(NOT_S_1));
  Transistor transistor_7 (.in(transistor_6_out), .out(Y_0), .gate(\YD_PRÓXIMO ));
  Transistor #(.\type ("n")) transistor_8 (.in(1'b0), .out(Y_0), .gate(\YD_PRÓXIMO ));
endmodule
