// Logisim project MEIO TR.circ as structural Verilog: 1 circuit, main circuit main
// MEIO
module main (
  input  D,
  input  S1,
  input  NOT_S1,
  input  YD_ANTERIOR,
  input  \YD_PRÓXIMO ,
  output S1_2,
  output NOT_S1_2,
  output DY_ANTERIOR,
  output \DY_PRÓXIMO ,
  output Y_1
);

  wire transistor_2_out, transistor_6_out, transistor_10_out;

  Transistor #(.\type ("n")) transistor_1 (.in(1'b0), .out(DY_ANTERIOR), .gate(NOT_S1));
  Transistor transistor_2 (.in(1'b1), .out(transistor_2_out), .gate(NOT_S1));
  Transistor transistor_3 (.in(transistor_2_out), .out(DY_ANTERIOR), .gate(D));
  Transistor #(.\type ("n")) transistor_4 (.in(1'b0), .out(DY_ANTERIOR), .gate(D));
  Transistor #(.\type ("n")) transistor_5 (.in(1'b0), .out(\DY_PRÓXIMO ), .gate(D));
  Transistor transistor_6 (.in(1'b1), .out(transistor_6_out), .gate(D));
  Transistor transistor_7 (.in(transistor_6_out), .out(\DY_PRÓXIMO ), .gate(S1));
  Transistor #(.\type ("n")) transistor_8 (.in(1'b0), .out(\DY_PRÓXIMO ), .gate(S1));
  Transistor #(.\type ("n")) transistor_9 (.in(1'b0), .out(Y_1), .gate(YD_ANTERIOR));
  Transistor transistor_10 (.in(1'b1), .out(transistor_10_out), .gate(YD_ANTERIOR));
  Transistor transistor_11 (.in(transistor_10_out), .out(Y_1), .gate(\YD_PRÓXIMO ));
  Transistor #(.\type ("n")) transistor_12 (.in(1'b0), .out(Y_1), .gate(\YD_PRÓXIMO ));

  assign NOT_S1_2 = NOT_S1;
  assign S1_2 = S1;
endmodule
