// Logisim project MUX 2 X 1 TR.circ as structural Verilog: 1 circuit, main circuit main
// MUX
module main (
  input  S,
  input  E_1,
  input  E_2,
  output Y
);

  wire transistor_1_out;

  Transistor transistor_1 (.in(1'b1), .out(transistor_1_out), .gate(S));
  Transistor #(.\type ("n")) transistor_2 (.in(1'b0), .out(transistor_1_out), .gate(S));
  // Transmission_Gate transmission_1: pin names not known; wires that end beside it: E_1, S, transistor_1_out, Y
  // Transmission_Gate transmission_2: pin names not known; wires that end beside it: E_2, transistor_1_out, S, Y
endmodule
