// Logisim project MUX 4 X 1 10 BITS TR.circ as structural Verilog: 1 circuit, main circuit main
// MUU 4 X 1 10 BITS TR
module main (
  input  D9,
  input  D8,
  input  D7,
  input  D6,
  input  D5,
  input  D4,
  input  D3,
  input  D2,
  input  D1,
  input  D0,
  input  C9,
  input  C8,
  input  C7,
  input  C6,
  input  C5,
  input  C4,
  input  C3,
  input  C2,
  input  C1,
  input  C0,
  input  B9,
  input  B8,
  input  B7,
  input  B6,
  input  B5,
  input  B4,
  input  B3,
  input  B2,
  input  B1,
  input  B0,
  input  A9,
  input  A8,
  input  A7,
  input  A6,
  input  A5,
  input  A4,
  input  A3,
  input  A2,
  input  A1,
  input  A0,
  input  S0,
  input  S1,
  output Q_9,
  output Q_8,
  output Q_7,
  output Q_6,
  output Q_5,
  output Q_4,
  output Q_3,
  output Q_2,
  output Q_1,
  output Q_0
);

  MUX_4_X_1_TR_main main_1 (.E_1(A9), .E_2(B9), .E_3(C9), .E_4(D9), .S_O(S0), .S_1(S1), .Y(Q_9));
  MUX_4_X_1_TR_main main_2 (.E_1(A8), .E_2(B8), .E_3(C8), .E_4(D8), .S_O(S0), .S_1(S1), .Y(Q_8));
  MUX_4_X_1_TR_main main_3 (.E_1(A7), .E_2(B7), .E_3(C7), .E_4(D7), .S_O(S0), .S_1(S1), .Y(Q_7));
  MUX_4_X_1_TR_main main_4 (.E_1(A6), .E_2(B6), .E_3(C6), .E_4(D6), .S_O(S0), .S_1(S1), .Y(Q_6));
  MUX_4_X_1_TR_main main_5 (.E_1(A5), .E_2(B5), .E_3(C5), .E_4(D5), .S_O(S0), .S_1(S1), .Y(Q_5));
  MUX_4_X_1_TR_main main_6 (.E_1(A4), .E_2(B4), .E_3(C4), .E_4(D4), .S_O(S0), .S_1(S1), .Y(Q_4));
  MUX_4_X_1_TR_main main_7 (.E_1(A3), .E_2(B3), .E_3(C3), .E_4(D3), .S_O(S0), .S_1(S1), .Y(Q_3));
  MUX_4_X_1_TR_main main_8 (.E_1(A2), .E_2(B2), .E_3(C2), .E_4(D2), .S_O(S0), .S_1(S1), .Y(Q_2));
  MUX_4_X_1_TR_main main_9 (.E_1(A1), .E_2(B1), .E_3(C1), .E_4(D1), .S_O(S0), .S_1(S1), .Y(Q_1));
  MUX_4_X_1_TR_main main_10 (.E_1(A0), .E_2(B0), .E_3(C0), .E_4(D0), .S_O(S0), .S_1(S1), .Y(Q_0));
endmodule
