// Logisim project MUX 4 X 1 TR.circ as structural Verilog: 1 circuit, main circuit main
// M 4X1
module main (
  input  S_O,
  input  S_1,
  input  E_1,
  input  E_2,
  input  E_3,
  input  E_4,
  output Y
);

  wire transmission_1_p3, transmission_1_p4, transmission_3_p3, transmission_4_p4, transmission_5_p3;

  // Transmission_Gate transmission_1: pin names not known; wires that end beside it: E_1, S_O, transmission_1_p3, transmission_1_p4
  Transistor transistor_1 (.in(1'b1), .out(transmission_1_p3), .gate(S_O));
  Transistor #(.\type ("n")) transistor_2 (.in(1'b0), .out(transmission_1_p3), .gate(S_O));
  // Transmission_Gate transmission_2: pin names not known; wires that end beside it: E_2, transmission_1_p3, S_O
  // Transmission_Gate transmission_3: pin names not known; wires that end beside it: E_3, S_O, transmission_3_p3
  Transistor transistor_3 (.in(1'b1), .out(transmission_3_p3), .gate(S_O));
  Transistor #(.\type ("n")) transistor_4 (.in(1'b0), .out(transmission_3_p3), .gate(S_O));
  // Transmission_Gate transmission_4: pin names not known; wires that end beside it: E_4, transmission_3_p3, S_O, transmission_4_p4
  // Transmission_Gate transmission_5: pin names not known; wires that end beside it: transmission_1_p4, S_1, transmission_5_p3, Y
  Transistor transistor_5 (.in(1'b1), .out(transmission_5_p3), .gate(S_1));
  Transistor #(.\type ("n")) transistor_6 (.in(1'b0), .out(transmission_5_p3), .gate(S_1));
  // Transmission_Gate transmission_6: pin names not known; wires that end beside it: transmission_4_p4, transmission_5_p3, S_1, Y
endmodule
