// Logisim project SST TR.circ as structural Verilog: 1 circuit, main circuit main
// SST
module main (
  input  Cin,
  input  A,
  input  B,
  input  S,
  output Q,
  output Cout
);

  wire transistor_1_out, transistor_4_out, transistor_5_out, transistor_8_out, transistor_9_out,
       transistor_12_out, transistor_13_out, transistor_16_out, transistor_20_out, transistor_24_out;

  Transistor #(.gate("br")) transistor_1 (.in(S), .out(transistor_1_out), .gate(B));
  Transistor transistor_2 (.in(B), .out(transistor_1_out), .gate(S));
  Transistor #(.\type ("n")) transistor_3 (.in(transistor_4_out), .out(transistor_1_out), .gate(S));
  Transistor #(.\type ("n")) transistor_4 (.in(1'b0), .out(transistor_4_out), .gate(B));
  Transistor transistor_5 (.in(1'b1), .out(transistor_5_out), .gate(transistor_1_out));
  Transistor transistor_6 (.in(1'b1), .out(transistor_5_out), .gate(A));
  Transistor #(.\type ("n")) transistor_7 (.in(transistor_8_out), .out(transistor_5_out), .gate(A));
  Transistor #(.\type ("n")) transistor_8 (.in(1'b0), .out(transistor_8_out), .gate(transistor_1_out));
  Transistor #(.gate("br")) transistor_9 (.in(A), .out(transistor_9_out), .gate(transistor_1_out));
  Transistor transistor_10 (.in(transistor_1_out), .out(transistor_9_out), .gate(A));
  Transistor #(.\type ("n")) transistor_11 (.in(transistor_12_out), .out(transistor_9_out), .gate(A));
  Transistor #(.\type ("n")) transistor_12 (.in(1'b0), .out(transistor_12_out), .gate(transistor_1_out));
  Transistor transistor_13 (.in(1'b1), .out(transistor_13_out), .gate(transistor_9_out));
  Transistor transistor_14 (.in(1'b1), .out(transistor_13_out), .gate(Cin));
  Transistor #(.\type ("n")) transistor_15 (.in(transistor_16_out), .out(transistor_13_out), .gate(transistor_9_out));
  Transistor #(.\type ("n")) transistor_16 (.in(1'b0), .out(transistor_16_out), .gate(Cin));
  Transistor #(.gate("br")) transistor_17 (.in(transistor_9_out), .out(Q), .gate(Cin));
  Transistor transistor_18 (.in(Cin), .out(Q), .gate(transistor_9_out));
  Transistor #(.\type ("n")) transistor_19 (.in(transistor_20_out), .out(Q), .gate(transistor_9_out));
  Transistor #(.\type ("n")) transistor_20 (.in(1'b0), .out(transistor_20_out), .gate(Cin));
  Transistor transistor_21 (.in(1'b1), .out(Cout), .gate(transistor_13_out));
  Transistor transistor_22 (.in(1'b1), .out(Cout), .gate(transistor_5_out));
  Transistor #(.\type ("n")) transistor_23 (.in(transistor_24_out), .out(Cout), .gate(transistor_13_out));
  Transistor #(.\type ("n")) transistor_24 (.in(1'b0), .out(transistor_24_out), .gate(transistor_5_out));
endmodule
