// Logisim project ULA 10 BITS TR.circ as structural Verilog: 1 circuit, main circuit main
module main (
  input  A0,
  input  B0,
  input  A1,
  input  B1,
  input  A2,
  input  B2,
  input  A3,
  input  B3,
  input  A4,
  input  B4,
  input  A5,
  input  B5,
  input  A6,
  input  B6,
  input  A7,
  input  B7,
  input  A8,
  input  B8,
  input  A9,
  input  B9,
  input  S0,
  input  S2,
  input  S1,
  input  S3,
  input  Cin,
  output Q_0,
  output Q_1,
  output Q_2,
  output Q_3,
  output Q_4,
  output Q_5,
  output Q_6,
  output Q_7,
  output Q_8,
  output Q_9,
  output A___B,
  output A___B_2,
  output A___B_3,
  output A___0,
  output B___0,
  output O_F,
  output Cout
);

  wire main_2_c_3, main_2_q_0, main_2_q_1, main_2_q_2, main_2_q_3, main_2_q_4, main_2_q_5, main_2_q_6,
       main_2_q_7, main_2_q_8, main_2_q_9, main_3_y_0, main_3_y_1, main_3_y_2, main_3_y_3, main_3_y_4,
       main_3_y_5, main_3_y_6, main_3_y_7, main_3_y_8, main_3_y_9, main_4_q_0, main_4_q_1, main_4_q_2,
       main_4_q_3, main_4_q_4, main_4_q_5, main_4_q_6, main_4_q_7, main_4_q_8, main_4_q_9, main_5_nand_0,
       main_5_nand_1, main_5_nand_2, main_5_nand_3, main_5_nand_4, main_5_nand_5, main_5_nand_6,
       main_5_nand_7, main_5_nand_8, main_5_nand_9, main_5_nor_0, main_5_nor_1, main_5_nor_2, main_5_nor_3,
       main_5_nor_4, main_5_nor_5, main_5_nor_6, main_5_nor_7, main_5_nor_8, main_5_nor_9, main_5_xor_0,
       main_5_xor_1, main_5_xor_2, main_5_xor_3, main_5_xor_4, main_5_xor_5, main_5_xor_6, main_5_xor_7,
       main_5_xor_8, main_5_xor_9, main_6_q_0, main_6_q_1, main_6_q_2, main_6_q_3, main_6_q_4, main_6_q_5,
       main_6_q_6, main_6_q_7, main_6_q_8, main_6_q_9, main_7_s_0, main_7_s_1, main_7_s_2, main_7_s_3,
       main_7_s_4, main_7_s_5, main_7_s_6, main_7_s_7, main_7_s_8, main_7_s_9;

  COMPARADOR_10_BITS_main main_1 (
    .C_8(main_2_c_3), .Cout(Cout), .B9(B9), .B8(B8), .B7(B7), .B6(B6), .B5(B5), .B4(B4), .B3(B3), .B2(B2),
    .B1(B1), .B0(B0), .A9(A9), .A8(A8), .A7(A7), .A6(A6), .A5(A5), .A4(A4), .A3(A3), .A2(A2), .A1(A1),
    .A0(A0), .Q9(main_2_q_9), .Q8(main_2_q_8), .Q7(main_2_q_7), .Q6(main_2_q_6), .Q5(main_2_q_5),
    .Q4(main_2_q_4), .Q3(main_2_q_3), .Q2(main_2_q_2), .Q1(main_2_q_1), .Q0(main_2_q_0), .OVER_FLOW(O_F),
    .B___0(B___0), .A___0(A___0), .A___B(A___B_3), .A___B_2(A___B_2), .A___B_3(A___B));
  \ARITMÉTICA_10_BITS_TR_main  main_2 (
    .B_9(B9), .A_9(A9), .B_8(B8), .A_8(A8), .B_7(B7), .A_7(A7), .B_6(B6), .A_6(A6), .B_5(B5), .A_5(A5),
    .B_4(B4), .A_4(A4), .B_3(B3), .A_3(A3), .B_2(B2), .A_2(A2), .B_1(B1), .A_1(A1), .B_0(B0), .A_0(A0),
    .Cin(Cin), .S_0(S0), .S_1(S1), .Cout(Cout), .C_3(main_2_c_3), .Q_9(main_2_q_9), .Q_8(main_2_q_8),
    .Q_7(main_2_q_7), .Q_6(main_2_q_6), .Q_5(main_2_q_5), .Q_4(main_2_q_4), .Q_3(main_2_q_3),
    .Q_2(main_2_q_2), .Q_1(main_2_q_1), .Q_0(main_2_q_0));
  DESLOCAMENTO_10_BITS_TR_main main_3 (
    .S_0(S0), .S1(S1), .D_9(A9), .D_8(A8), .D_7(A7), .D_6(A6), .D_5(A5), .D_4(A4), .D_3(A3), .D_2(A2),
    .D_1(A1), .D_0(A0), .Y_9(main_3_y_9), .Y_8(main_3_y_8), .Y_7(main_3_y_7), .Y_6(main_3_y_6),
    .Y_5(main_3_y_5), .Y_4(main_3_y_4), .Y_3(main_3_y_3), .Y_2(main_3_y_2), .Y_1(main_3_y_1), .Y_0(main_3_y_0));
  MUX_2_X_1_10_BITS_TR_main main_4 (
    .B9(main_2_q_9), .B8(main_2_q_8), .B7(main_2_q_7), .B6(main_2_q_6), .B5(main_2_q_5), .B4(main_2_q_4),
    .B3(main_2_q_3), .B2(main_2_q_2), .B1(main_2_q_1), .B0(main_2_q_0), .A9(main_3_y_9), .A8(main_3_y_8),
    .A7(main_3_y_7), .A6(main_3_y_6), .A5(main_3_y_5), .A4(main_3_y_4), .A3(main_3_y_3), .A2(main_3_y_2),
    .A1(main_3_y_1), .A0(main_3_y_0), .Q_9(main_4_q_9), .Q_8(main_4_q_8), .Q_7(main_4_q_7), .Q_6(main_4_q_6),
    .Q_5(main_4_q_5), .Q_4(main_4_q_4), .Q_3(main_4_q_3), .Q_2(main_4_q_2), .Q_1(main_4_q_1),
    .Q_0(main_4_q_0), .S(S2));
  BIT_A_BIT_10_BITS_TR_main main_5 (
    .B_9(B9), .A_9(A9), .B_8(B8), .A_8(A8), .B_7(B7), .A_7(A7), .B_6(B6), .A_6(A6), .B_5(B5), .A_5(A5),
    .B_4(B4), .A_4(A4), .B_3(B3), .A_3(A3), .B_2(B2), .A_2(A2), .B_1(B1), .A_1(A1), .B_0(B0), .A_0(A0),
    .XOR_9(main_5_xor_9), .XOR_8(main_5_xor_8), .XOR_7(main_5_xor_7), .XOR_6(main_5_xor_6),
    .XOR_5(main_5_xor_5), .XOR_4(main_5_xor_4), .XOR_3(main_5_xor_3), .XOR_2(main_5_xor_2),
    .XOR_1(main_5_xor_1), .XOR_0(main_5_xor_0), .NOR_9(main_5_nor_9), .NOR_8(main_5_nor_8),
    .NOR_7(main_5_nor_7), .NOR_6(main_5_nor_6), .NOR_5(main_5_nor_5), .NOR_4(main_5_nor_4),
    .NOR_3(main_5_nor_3), .NOR_2(main_5_nor_2), .NOR_1(main_5_nor_1), .NOR_0(main_5_nor_0),
    .NAND_9(main_5_nand_9), .NAND_8(main_5_nand_8), .NAND_7(main_5_nand_7), .NAND_6(main_5_nand_6),
    .NAND_5(main_5_nand_5), .NAND_4(main_5_nand_4), .NAND_3(main_5_nand_3), .NAND_2(main_5_nand_2),
    .NAND_1(main_5_nand_1), .NAND_0(main_5_nand_0));
  MUX_4_X_1_10_BITS_TR_main main_6 (
    .S0(S0), .S1(S1), .D9(main_5_xor_9), .D8(main_5_xor_8), .D7(main_5_xor_7), .D6(main_5_xor_6),
    .D5(main_5_xor_5), .D4(main_5_xor_4), .D3(main_5_xor_3), .D2(main_5_xor_2), .D1(main_5_xor_1),
    .D0(main_5_xor_0), .C9(main_5_nor_9), .C8(main_5_nor_8), .C7(main_5_nor_7), .C6(main_5_nor_6),
    .C5(main_5_nor_5), .C4(main_5_nor_4), .C3(main_5_nor_3), .C2(main_5_nor_2), .C1(main_5_nor_1),
    .C0(main_5_nor_0), .B9(main_5_nand_9), .B8(main_5_nand_8), .B7(main_5_nand_7), .B6(main_5_nand_6),
    .B5(main_5_nand_5), .B4(main_5_nand_4), .B3(main_5_nand_3), .B2(main_5_nand_2), .B1(main_5_nand_1),
    .B0(main_5_nand_0), .A9(A9), .A8(A8), .A7(A7), .A6(A6), .A5(A5), .A4(A4), .A3(A3), .A2(A2), .A1(A1),
    .A0(A0), .Q_9(main_6_q_9), .Q_8(main_6_q_8), .Q_7(main_6_q_7), .Q_6(main_6_q_6), .Q_5(main_6_q_5),
    .Q_4(main_6_q_4), .Q_3(main_6_q_3), .Q_2(main_6_q_2), .Q_1(main_6_q_1), .Q_0(main_6_q_0));
  XOR_10_BITS_TR_main main_7 (
    .A_8(main_6_q_0), .A_7(main_6_q_1), .A_6(main_6_q_2), .A_5(main_6_q_3), .A_4(main_6_q_4),
    .A_4_2(main_6_q_5), .A_3(main_6_q_6), .A_2(main_6_q_7), .A_1(main_6_q_8), .A_0(main_6_q_9), .S(S2),
    .S_0(main_7_s_0), .S_1(main_7_s_1), .S_2(main_7_s_2), .S_3(main_7_s_3), .S_4(main_7_s_4),
    .S_5(main_7_s_5), .S_6(main_7_s_6), .S_7(main_7_s_7), .S_8(main_7_s_8), .S_9(main_7_s_9));
  MUX_2_X_1_10_BITS_TR_main main_8 (
    .B9(main_4_q_9), .B8(main_4_q_8), .B7(main_4_q_7), .B6(main_4_q_6), .B5(main_4_q_5), .B4(main_4_q_4),
    .B3(main_4_q_3), .B2(main_4_q_2), .B1(main_4_q_1), .B0(main_4_q_0), .A9(main_7_s_9), .A8(main_7_s_8),
    .A7(main_7_s_7), .A6(main_7_s_6), .A5(main_7_s_5), .A4(main_7_s_4), .A3(main_7_s_3), .A2(main_7_s_2),
    .A1(main_7_s_1), .A0(main_7_s_0), .Q_9(Q_9), .Q_8(Q_8), .Q_7(Q_7), .Q_6(Q_6), .Q_5(Q_5), .Q_4(Q_4),
    .Q_3(Q_3), .Q_2(Q_2), .Q_1(Q_1), .Q_0(Q_0), .S(S3));
endmodule
