// Logisim project XOR 10 BITS TR.circ as structural Verilog: 1 circuit, main circuit main
// XOR TR
module main (
  input  A_8,
  input  A_7,
  input  A_6,
  input  A_5,
  input  A_4,
  input  A_4_2,
  input  A_3,
  input  A_2,
  input  A_1,
  input  A_0,
  input  S,
  output S_0,
  output S_1,
  output S_2,
  output S_3,
  output S_4,
  output S_5,
  output S_6,
  output S_7,
  output S_8,
  output S_9
);

  wire transistor_4_out, transistor_8_out, transistor_12_out, transistor_16_out, transistor_20_out,
       transistor_24_out, transistor_28_out, transistor_32_out, transistor_36_out, transistor_40_out;

  Transistor #(.gate("br")) transistor_1 (.in(A_0), .out(S_0), .gate(S));
  Transistor transistor_2 (.in(S), .out(S_0), .gate(A_0));
  Transistor #(.\type ("n")) transistor_3 (.in(transistor_4_out), .out(S_0), .gate(A_0));
  Transistor #(.\type ("n")) transistor_4 (.in(1'b0), .out(transistor_4_out), .gate(S));
  Transistor #(.gate("br")) transistor_5 (.in(A_1), .out(S_1), .gate(S));
  Transistor transistor_6 (.in(S), .out(S_1), .gate(A_1));
  Transistor #(.\type ("n")) transistor_7 (.in(transistor_8_out), .out(S_1), .gate(A_1));
  Transistor #(.\type ("n")) transistor_8 (.in(1'b0), .out(transistor_8_out), .gate(S));
  Transistor #(.gate("br")) transistor_9 (.in(A_2), .out(S_2), .gate(S));
  Transistor transistor_10 (.in(S), .out(S_2), .gate(A_2));
  Transistor #(.\type ("n")) transistor_11 (.in(transistor_12_out), .out(S_2), .gate(A_2));
  Transistor #(.\type ("n")) transistor_12 (.in(1'b0), .out(transistor_12_out), .gate(S));
  Transistor #(.gate("br")) transistor_13 (.in(A_3), .out(S_3), .gate(S));
  Transistor transistor_14 (.in(S), .out(S_3), .gate(A_3));
  Transistor #(.\type ("n")) transistor_15 (.in(transistor_16_out), .out(S_3), .gate(A_3));
  Transistor #(.\type ("n")) transistor_16 (.in(1'b0), .out(transistor_16_out), .gate(S));
  Transistor #(.gate("br")) transistor_17 (.in(A_4_2), .out(S_4), .gate(S));
  Transistor transistor_18 (.in(S), .out(S_4), .gate(A_4_2));
  Transistor #(.\type ("n")) transistor_19 (.in(transistor_20_out), .out(S_4), .gate(A_4_2));
  Transistor #(.\type ("n")) transistor_20 (.in(1'b0), .out(transistor_20_out), .gate(S));
  Transistor #(.gate("br")) transistor_21 (.in(A_4), .out(S_5), .gate(S));
  Transistor transistor_22 (.in(S), .out(S_5), .gate(A_4));
  Transistor #(.\type ("n")) transistor_23 (.in(transistor_24_out), .out(S_5), .gate(A_4));
  Transistor #(.\type ("n")) transistor_24 (.in(1'b0), .out(transistor_24_out), .gate(S));
  Transistor #(.gate("br")) transistor_25 (.in(A_5), .out(S_6), .gate(S));
  Transistor transistor_26 (.in(S), .out(S_6), .gate(A_5));
  Transistor #(.\type ("n")) transistor_27 (.in(transistor_28_out), .out(S_6), .gate(A_5));
  Transistor #(.\type ("n")) transistor_28 (.in(1'b0), .out(transistor_28_out), .gate(S));
  Transistor #(.gate("br")) transistor_29 (.in(A_6), .out(S_7), .gate(S));
  Transistor transistor_30 (.in(S), .out(S_7), .gate(A_6));
  Transistor #(.\type ("n")) transistor_31 (.in(transistor_32_out), .out(S_7), .gate(A_6));
  Transistor #(.\type ("n")) transistor_32 (.in(1'b0), .out(transistor_32_out), .gate(S));
  Transistor #(.gate("br")) transistor_33 (.in(A_7), .out(S_8), .gate(S));
  Transistor transistor_34 (.in(S), .out(S_8), .gate(A_7));
  Transistor #(.\type ("n")) transistor_35 (.in(transistor_36_out), .out(S_8), .gate(A_7));
  Transistor #(.\type ("n")) transistor_36 (.in(1'b0), .out(transistor_36_out), .gate(S));
  Transistor #(.gate("br")) transistor_37 (.in(A_8), .out(S_9), .gate(S));
  Transistor transistor_38 (.in(S), .out(S_9), .gate(A_8));
  Transistor #(.\type ("n")) transistor_39 (.in(transistor_40_out), .out(S_9), .gate(A_8));
  Transistor #(.\type ("n")) transistor_40 (.in(1'b0), .out(transistor_40_out), .gate(S));
endmodule
